# Fritzing sketch Representacao Grafica - Display (saved by Fritzing 0.9.3b)
breadboards: 1

parts:
  Arduino1 = Arduino Uno (Rev3)
  NRF24L3 = NRF24L01
  R3 = Resistor [tolerance=±5% resistance=220 package=THT]
  GLCD_128x1 = 128 x 64 Graphic LCD
  RE1 = Rotary Encoder [package=THT]
  S3 = Pushbutton [package="[THT]"]
  S4 = Pushbutton [package="[THT]"]
  S5 = Pushbutton [package="[THT]"]
  R4 = Resistor [tolerance=±5% resistance=220 package=THT]
  R5 = Resistor [tolerance=±5% resistance=220 package=THT]

nets:
  N1: Arduino1.A0, S5.Pin_1, S5.Pin_2, R4.Pin_1
  N2: Arduino1.A1, RE1.EncoderPinC
  N3: Arduino1.D8, GLCD_128x1.4_D/I
  N4: Arduino1.D9_PWM, GLCD_128x1.5_R/W
  N5: Arduino1.D10_PWM/SS, GLCD_128x1.6_Enable
  N6: Arduino1.D11_PWM/MOSI, NRF24L3.MOSI
  N7: Arduino1.D12/MISO, NRF24L3.MISO
  N8: Arduino1.D13/SCK, NRF24L3.SCK
  N9: Arduino1.D2, R3.Pin_1, S3.Pin_1, S3.Pin_2
  N10: Arduino1.D3_PWM, NRF24L3.CSN
  N11: Arduino1.D4, GLCD_128x1.17_RST
  N12: Arduino1.D5_PWM, GLCD_128x1.19_A(+)
  N13: Arduino1.D6_PWM, S4.Pin_1, S4.Pin_2, R5.Pin_1
  N14: Arduino1.D7, NRF24L3.CE
  3V3: Arduino1.3V3, NRF24L3.VCC
  N15: Arduino1.5V, R3.Pin_0, GLCD_128x1.2_Vdd, RE1.EncoderPinB, R4.Pin_0, R5.Pin_0
  GND: Arduino1.GND, NRF24L3.GND, GLCD_128x1.1_Vss, GLCD_128x1.16_CS2, GLCD_128x1.20_K(-), RE1.EncoderPinA, S3.Pin_3, S3.Pin_4, S4.Pin_3, S4.Pin_4, S5.Pin_3, S5.Pin_4

notes:
  BLINK
  GND = Black
  VCC = Red
  CE = Yellow
  CSN = Green
  SCK = Orange
  MOSI = White
  MISO = Brown
  IRQ = Not Connected
  Modo Manual
  Liga/Desl Bomba
  Liga/Desl Sistema

custom parts:
  NRF24L01: NRF24L01 module

// code stored in the sketch: Blink.ino
/*
  Blink
  
  Switching a LED on and off
  
  This example is part of the Fritzing Creator Kit: www.fritzing.org/creator-kit.
*/

int led = 13;                   // integer variable led is declared

void setup() {                  // the setup() method is executed only once
  pinMode(led, OUTPUT);         // the led PIN is declared as digital output
}

void loop() {                   // the loop() method is repeated
  digitalWrite(led, HIGH);      // switching on the led 
  delay(1000);                  // stopping the program for 1000 milliseconds
  digitalWrite(led, LOW);       // switching off the led 
  delay(1000);                  // stopping the program for 1000 milliseconds
}
