# Fritzing sketch Representacao Grafica - Sensor Ultrasonico (saved by Fritzing 0.9.3b)
breadboards: 1

parts:
  Arduino1 = Arduino Uno (Rev3)
  U3 = HC-SR04 [chip_label=IC package="SIP (Single Inline) [THT]"]  # not connected
  NRF24L3 = NRF24L01
  LED2 = smd LED [color="Yellow (595nm)" package="1206 [SMD]"]
  R3 = Resistor [tolerance=±5% resistance=220 package=THT]

nets:
  N1: Arduino1.D8, NRF24L3.CE
  N2: Arduino1.D9_PWM, NRF24L3.CSN
  N3: Arduino1.D11_PWM/MOSI, NRF24L3.MOSI
  N4: Arduino1.D12/MISO, NRF24L3.MISO
  N5: Arduino1.D13/SCK, NRF24L3.SCK
  3V3: Arduino1.3V3, NRF24L3.VCC
  N6: Arduino1.5V, R3.Pin_1
  GND: Arduino1.GND, NRF24L3.GND, LED2.cathode
  N7: LED2.anode, R3.Pin_0

notes:
  BLINK
  GND = Black
  VCC = Red
  CE = Yellow
  CSN = Green
  SCK = Orange
  MOSI = White
  MISO = Brown
  IRQ = Not Connected

custom parts:
  HC-SR04: HC-SR04 ultrasound distance sensor
  NRF24L01: NRF24L01 module

// code stored in the sketch: Blink.ino
/*
  Blink
  
  Switching a LED on and off
  
  This example is part of the Fritzing Creator Kit: www.fritzing.org/creator-kit.
*/

int led = 13;                   // integer variable led is declared

void setup() {                  // the setup() method is executed only once
  pinMode(led, OUTPUT);         // the led PIN is declared as digital output
}

void loop() {                   // the loop() method is repeated
  digitalWrite(led, HIGH);      // switching on the led 
  delay(1000);                  // stopping the program for 1000 milliseconds
  digitalWrite(led, LOW);       // switching off the led 
  delay(1000);                  // stopping the program for 1000 milliseconds
}
