# Fritzing sketch Representacao Grafica - Tarefa_2_Sensores_atuadoresV2 (saved by Fritzing 0.9.3b)
breadboards: 1

parts:
  Arduino1 = Arduino Uno (Rev3)
  LED1 = smd LED [color="Red (633nm)" package="0603 [SMD]"]
  LED1_2 = smd LED [color="Yellow (595nm)" package="1206 [SMD]"]
  R1 = Resistor [tolerance=±5% resistance=220 package=THT]
  R2 = Resistor [tolerance=±5% resistance=220 package=THT]
  S1 = Pushbutton [package="[THT]"]
  S2 = Pushbutton [package="[THT]"]
  R3 = Resistor [tolerance=±5% resistance=220 package=THT]
  R4 = Resistor [tolerance=±5% resistance=220 package=THT]
  R5 = Photocell (LDR) [package=THT]
  R6 = Resistor [tolerance=±5% resistance=220 package=THT]
  J1 = Piezo Speaker
  U3 = HC-SR04 [chip_label=IC package="SIP (Single Inline) [THT]"]  # not connected

nets:
  N1: Arduino1.A5/SCL, R5.pin_1, R6.Pin_0
  N2: Arduino1.D10_PWM/SS, R1.Pin_1
  N3: Arduino1.D13/SCK, LED1_2.anode, R2.Pin_0
  N4: Arduino1.GND, S1.Pin_1, S1.Pin_2, S2.Pin_1, S2.Pin_2, J1.pin1
  N5: Arduino1.D2, S2.Pin_3, S2.Pin_4, R4.Pin_1
  N6: Arduino1.D4, S1.Pin_3, S1.Pin_4, R3.Pin_1
  N7: Arduino1.D5_PWM, J1.pin2
  N8: Arduino1.5V, R3.Pin_0, R4.Pin_0, R6.Pin_1
  N9: LED1.cathode, LED1_2.cathode, R5.pin_0
  N10: LED1.anode, R1.Pin_0

notes:
  BLINK

custom parts:
  HC-SR04: HC-SR04 ultrasound distance sensor

// code stored in the sketch: Blink.ino
/*
  Blink
  
  Switching a LED on and off
  
  This example is part of the Fritzing Creator Kit: www.fritzing.org/creator-kit.
*/

int led = 13;                   // integer variable led is declared

void setup() {                  // the setup() method is executed only once
  pinMode(led, OUTPUT);         // the led PIN is declared as digital output
}

void loop() {                   // the loop() method is repeated
  digitalWrite(led, HIGH);      // switching on the led 
  delay(1000);                  // stopping the program for 1000 milliseconds
  digitalWrite(led, LOW);       // switching off the led 
  delay(1000);                  // stopping the program for 1000 milliseconds
}
